// Logisim project ex4.circ as structural Verilog: 5 circuits, main circuit RotRight
module RotRight (
  input  [15:0] INPUT0,
  input  [3:0] AMOUNT,
  output [15:0] OUTPUT0,
  output [15:0] out_4,
  output [15:0] out_5,
  output [15:0] out_6
);

  wire [15:0] rot1_1_out_2, rot2_1_out_2, rot4_1_out_2, rot8_1_out_2;

  rot4 rot4_1 (.in_1(out_5), .out_2(rot4_1_out_2));
  rot8 rot8_1 (.in_1(out_6), .out_2(rot8_1_out_2));
  rot1 rot1_1 (.in_1(INPUT0), .out_2(rot1_1_out_2));
  Multiplexer #(.width(16)) multiplexer_1 (.in0(out_4), .in1(rot2_1_out_2), .out(out_5), .sel(AMOUNT[1]));
  rot2 rot2_1 (.in_1(out_4), .out_2(rot2_1_out_2));
  Multiplexer #(.width(16)) multiplexer_2 (.in0(out_5), .in1(rot4_1_out_2), .out(out_6), .sel(AMOUNT[2]));
  Multiplexer #(.width(16)) multiplexer_3 (.in0(out_6), .in1(rot8_1_out_2), .out(OUTPUT0), .sel(AMOUNT[3]));
  Multiplexer #(.width(16)) multiplexer_4 (.in0(INPUT0), .in1(rot1_1_out_2), .out(out_4), .sel(AMOUNT[0]));

  // Other names for the same wires on the sheet: AMT0[3:0] = AMOUNT; AMT1[2:0] = AMOUNT[3:1]; AMT2[1:0] = AMOUNT[3:2];
  //   AMT3 = AMOUNT[3]; INP0[15:0] = INPUT0; INP1[15:0] = out_4; INP2[15:0] = out_5; INP3[15:0] = out_6;
  //   INP4[15:0] = OUTPUT0
endmodule

module rot1 (
  input  [15:0] in_1,
  output [15:0] out_2
);

  wire [15:0] SR;

  assign SR = {{1{1'b0}}, in_1[15:1]};  // Bit_Extender bit_extender_1
  assign out_2 = {in_1[0], {15{1'b0}}} | SR;  // OR_Gate or_1, 16 bits wide

  // Other names for the same wires on the sheet: INP[15:0] = in_1; ROT[15:0] = out_2; LOW = in_1[0]; SL[15] = in_1[0]
endmodule

module rot2 (
  input  [15:0] in_1,
  output [15:0] out_2
);

  wire [15:0] SR;

  assign SR = {{2{1'b0}}, in_1[15:2]};  // Bit_Extender bit_extender_1
  assign out_2 = {in_1[1:0], {14{1'b0}}} | SR;  // OR_Gate or_1, 16 bits wide

  // Other names for the same wires on the sheet: INP[15:0] = in_1; SL[15:14] = in_1[1:0]
endmodule

module rot4 (
  input  [15:0] in_1,
  output [15:0] out_2
);

  wire [15:0] SR;

  assign SR = {{4{1'b0}}, in_1[15:4]};  // Bit_Extender bit_extender_1
  assign out_2 = SR | {in_1[3:0], {12{1'b0}}};  // OR_Gate or_1, 16 bits wide

  // Other names for the same wires on the sheet: INP[15:0] = in_1; SL[15:12] = in_1[3:0]
endmodule

module rot8 (
  input  [15:0] in_1,
  output [15:0] out_2
);

  wire [15:0] bit_extender_1_out;

  assign bit_extender_1_out = {{8{1'b0}}, in_1[15:8]};  // Bit_Extender bit_extender_1
  assign out_2 = bit_extender_1_out | {in_1[7:0], {8{1'b0}}};  // OR_Gate or_1, 16 bits wide

  // Other names for the same wires on the sheet: INP[15:0] = in_1
endmodule
