// Logisim project ex2.circ as structural Verilog: 1 circuit, main circuit compute_BrUn
module compute_BrUn (
  input  [31:0] INSTRUCTION,
  output BrUn
);

  wire comparator_2_eq, comparator_2_gt, comparator_2_lt, DC, ISSB, NOSB1, NOSB2, or_1_out, or_3_out;

  Comparator #(.mode("unsigned"), .width(7)) comparator_1 (
    .a(INSTRUCTION[6:0]), .b(7'b1100111), .gt(NOSB1), .eq(ISSB), .lt(NOSB2));
  Comparator #(.mode("unsigned"), .width(3)) comparator_2 (
    .a(INSTRUCTION[14:12]), .b(3'b001), .gt(comparator_2_gt), .eq(comparator_2_eq), .lt(comparator_2_lt));
  and and_1 (BrUn, INSTRUCTION[13], comparator_2_gt);
  or or_1 (or_1_out, comparator_2_eq, comparator_2_lt);
  or or_2 (DC, or_1_out, or_3_out);
  or or_3 (or_3_out, NOSB1, NOSB2);

  // Other names for the same wires on the sheet: OP[6:0] = INSTRUCTION[6:0];
  //   IM[11:0] = {INSTRUCTION[31:25], INSTRUCTION[11:7]}; RI[24:0] = INSTRUCTION[31:7];
  //   funct3[2:0] = INSTRUCTION[14:12]; rs1[4:0] = INSTRUCTION[19:15]; rs2[4:0] = INSTRUCTION[24:20]; US = BrUn
endmodule
